# Fritzing sketch esquema_cesta (saved by Fritzing 0.9.3b)
breadboards: 1

parts:
  Componente1 = Arduino Uno (Rev3)
  HC-1 = HC-12 Module
  HC-2 = HC-12 Module
  buz1 = Piezo Buzzer
  Antenna2 = HC-12 Antenna
  HC-SR04_Sensor_1 = HC-SR04 Ultrasonic Distance Sensor
  S1 = Pushbutton [package="[THT]"]
  R1 = Resistor [tolerance=±5% resistance=220 package=THT]
  Antenna1 = HC-12 Antenna

nets:
  N1: Componente1.D8, HC-SR04_Sensor_1.TRIG
  N2: Componente1.D9_PWM, HC-SR04_Sensor_1.ECHO
  N3: Componente1.D10_PWM/SS, HC-1.RXD
  N4: Componente1.D11_PWM/MOSI, HC-1.TXD
  N5: Componente1.D2, S1.Pin_1, S1.Pin_2, R1.Pin_1
  N6: Componente1.D5_PWM, HC-2.RXD
  N7: Componente1.D6_PWM, HC-2.TXD
  N8: Componente1.D7, buz1.pin_2
  VCC: Componente1.5V, HC-1.VCC, HC-2.VCC, HC-SR04_Sensor_1.VCC, R1.Pin_0
  GND: Componente1.GND, HC-1.GND, HC-2.GND, buz1.pin_1, HC-SR04_Sensor_1.GND, S1.Pin_3, S1.Pin_4
  N9: HC-1.ANT, Antenna1.ANT
  N10: HC-2.ANT, Antenna2.ANT

custom parts:
  HC-12 Module: HC-12 433Mhz Module
  Piezo Buzzer: Part from https://www.nutsvolts.com/magazine/article/november2012_SmileysWorkshop modified to be .3 in spacing to match the adafruit buzzer 5V breadboard friendly part.
  HC-12 Antenna: Antenna for HC-12 433Mhz Module
