# Fritzing sketch novo_esquema_cesta (saved by Fritzing 0.9.2b)

parts:
  Componente1 = SRF05 Ultrasonic Rangefinder
  Componente2 = Arduino Uno (Rev3)
  HC-1 = HC-12 Module
  Antenna1 = HC-12 Antenna  # not connected

nets:
  VCC: Componente1.VCC, Componente2.5V
  N1: Componente1.Trig, Componente2.D9_PWM
  N2: Componente1.Echo, Componente2.D8
  GND: Componente1.GND, Componente2.GND, HC-1.GND
  N3: Componente2.D10_PWM/SS, HC-1.RXD
  N4: Componente2.D11_PWM/MOSI, HC-1.TXD
  3V3: Componente2.3V3, HC-1.VCC

custom parts:
  HC-12 Module: HC-12 433Mhz Module
  HC-12 Antenna: Antenna for HC-12 433Mhz Module
