# Fritzing sketch esquema_placar (saved by Fritzing 0.9.3b)
breadboards: 1

parts:
  Componente1 = Arduino Uno (Rev3)
  LED1 = LED - 5mm [color="Red (633nm)" package="5 mm [THT]"]
  LED2 = LED - 5mm [color="Green (570nm)" package="5 mm [THT]"]
  HC-1 = HC-12 Module
  Antenna1 = HC-12 Antenna

nets:
  N1: Componente1.D10_PWM/SS, HC-1.TXD
  N2: Componente1.D11_PWM/MOSI, HC-1.RXD
  N3: Componente1.D3_PWM, LED1.anode
  N4: Componente1.D4, LED2.anode
  5V: Componente1.5V, HC-1.VCC
  GND: Componente1.GND, LED1.cathode, LED2.cathode, HC-1.GND
  N5: HC-1.ANT, Antenna1.ANT

custom parts:
  HC-12 Module: HC-12 433Mhz Module
  HC-12 Antenna: Antenna for HC-12 433Mhz Module
