# Fritzing sketch emissor_esquema (saved by Fritzing 0.9.3b)
breadboards: 1

parts:
  Componente1 = Arduino Uno (Rev3)
  HC-1 = HC-12 Module
  Antenna1 = HC-12 Antenna
  R1 = Resistor [tolerance=±5% resistance=220 package=THT]
  S1 = Pushbutton [package="[THT]"]

nets:
  N1: Componente1.D10_PWM/SS, HC-1.TXD
  N2: Componente1.D11_PWM/MOSI, HC-1.RXD
  GND: Componente1.GND, HC-1.GND, S1.Pin_1, S1.Pin_2
  5V: Componente1.D4, Componente1.5V, HC-1.VCC, R1.Pin_0
  N3: HC-1.ANT, Antenna1.ANT
  N4: R1.Pin_1, S1.Pin_3, S1.Pin_4

custom parts:
  HC-12 Module: HC-12 433Mhz Module
  HC-12 Antenna: Antenna for HC-12 433Mhz Module
