# Fritzing sketch receptor_esquema (saved by Fritzing 0.9.3b)
breadboards: 1

parts:
  Componente2 = Arduino Uno (Rev3)
  HC-2 = HC-12 Module
  Antenna2 = HC-12 Antenna
  R2 = Resistor [tolerance=±5% resistance=220 package=THT]
  LED1 = LED - 5mm [color="Red (633nm)" package="5 mm [THT]"]

nets:
  N1: Componente2.D10_PWM/SS, HC-2.TXD
  N2: Componente2.D11_PWM/MOSI, HC-2.RXD
  N3: Componente2.D13/SCK, R2.Pin_0
  GND: Componente2.GND, HC-2.GND, LED1.anode
  5V: Componente2.5V, HC-2.VCC
  N4: HC-2.ANT, Antenna2.ANT
  N5: R2.Pin_1, LED1.cathode

custom parts:
  HC-12 Module: HC-12 433Mhz Module
  HC-12 Antenna: Antenna for HC-12 433Mhz Module
